# Fritzing sketch BME 280 SOLO (saved by Fritzing 1.0.4)
breadboards: 1

parts:
  M1 = BME280
  A1 = Esp32-c3 super mini

nets:
  N1: M1.VIN, A1.Pin_16
  N2: M1.GND, A1.Pin_15
  N3: M1.SCL, A1.Pin_5
  N4: M1.SDA, A1.Pin_4

custom parts:
  BME280: Temperature Humidity Barometric presure Sensor
  Esp32-c3 super mini: ESP32-C3 Development Board ESP32 SuperMini Development Board ESP32 Development Board WiFi Bluetooth.
