# Fritzing sketch DS18B20 EXPERIMENT (saved by Fritzing 1.0.4)
breadboards: 1

parts:
  DS1 = DS18B20 1-Wire Temperature Sensor Probe
  R1 = Resistor [tolerance=±5% resistance=10k package="0603 [SMD]"]
  Part1 = Arduino Uno (Rev3)
  R2 = Resistor [tolerance=±5% resistance=10k package="0603 [SMD]"]

nets:
  GND: DS1.GND, Part1.GND
  N1: DS1.DQ, R1.Pin_1, Part1.D2, R2.Pin_1
  VDD: DS1.VDD, R1.Pin_0, Part1.5V, R2.Pin_0
