# Fritzing sketch DS18B20 SOLO (saved by Fritzing 1.0.4)
breadboards: 1

parts:
  DS1 = DS18B20 1-Wire Temperature Sensor Probe
  A1 = Esp32-c3 super mini
  DS2 = DS18B20 1-Wire Temperature Sensor Probe
  DS3 = DS18B20 1-Wire Temperature Sensor Probe
  R1 = Resistor [tolerance=±5% resistance=4.7k package="0603 [SMD]"]

nets:
  GND: DS1.GND, A1.Pin_2, A1.Pin_11, DS2.GND, DS3.GND
  N1: DS1.DQ, DS2.DQ, DS3.DQ, R1.Pin_1
  VDD: DS1.VDD, A1.Pin_8, DS2.VDD, DS3.VDD, R1.Pin_0
  N2: A1.Pin_13, A1.Pin_15

custom parts:
  Esp32-c3 super mini: ESP32-C3 Development Board ESP32 SuperMini Development Board ESP32 Development Board WiFi Bluetooth.
