# Fritzing sketch MPU6050 (saved by Fritzing 1.0.4)

parts:
  A1 = Esp32-c3 super mini
  Part1 = InvenSense MPU6050

nets:
  N1: A1.Pin_4, Part1.SDA
  N2: A1.Pin_5, Part1.SCL
  N3: A1.Pin_15, Part1.GND
  N4: A1.Pin_16, Part1.VCC

custom parts:
  Esp32-c3 super mini: ESP32-C3 Development Board ESP32 SuperMini Development Board ESP32 Development Board WiFi Bluetooth.
