# Fritzing sketch RMS Prototype Ver 1 (saved by Fritzing 1.0.4)
breadboards: 1

parts:
  DS1 = DS18B20 1-Wire Temperature Sensor Probe
  A1 = Esp32-c3 super mini
  DS2 = DS18B20 1-Wire Temperature Sensor Probe
  DS3 = DS18B20 1-Wire Temperature Sensor Probe
  R1 = Resistor [tolerance=±5% resistance=4.7k package="0603 [SMD]"]
  M1 = BME280

nets:
  GND: DS1.GND, DS2.GND, DS3.GND, M1.GND
  N1: DS1.DQ, A1.Pin_9, DS2.DQ, DS3.DQ, R1.Pin_1
  VDD: DS1.VDD, DS2.VDD, DS3.VDD, R1.Pin_0, M1.VIN
  N2: A1.Pin_2, A1.Pin_11
  N3: A1.Pin_5, M1.SDA
  N4: A1.Pin_6, M1.SCL
  N5: A1.Pin_13, A1.Pin_15

custom parts:
  Esp32-c3 super mini: ESP32-C3 Development Board ESP32 SuperMini Development Board ESP32 Development Board WiFi Bluetooth.
  BME280: Temperature Humidity Barometric presure Sensor
