# Fritzing sketch TFT Display (saved by Fritzing 1.0.4)

parts:
  A1 = Esp32-c3 super mini
  IC1 = 2.8 inch LCD SPI display with touch screen & SD card

nets:
  N1: A1.Pin_1, IC1.SDO_(MISO), IC1.T_DO
  N2: A1.Pin_2, IC1.SDI_(MOSI), IC1.T_DIN
  N3: A1.Pin_3, IC1.CS
  N4: A1.Pin_4, IC1.T_CS
  N5: A1.Pin_11, IC1.DC
  N6: A1.Pin_12, IC1.RESET
  N7: A1.Pin_13, IC1.SCK, IC1.T_CLK
  N8: A1.Pin_14, IC1.LED
  N9: A1.Pin_15, IC1.GND
  N10: A1.Pin_16, IC1.VCC

custom parts:
  Esp32-c3 super mini: ESP32-C3 Development Board ESP32 SuperMini Development Board ESP32 Development Board WiFi Bluetooth.
  2.8 inch LCD SPI display with touch screen & SD card: A generic 2.8 inch LCD TFT 320x280 display with touchscreen and SD card slot.
